// Logisim project ALU.circ as structural Verilog: 1 circuit, main circuit ALU
module ALU (
  input  [31:0] A,
  input  [31:0] B,
  input  [4:0] Shift,
  input  CarryIn,
  input  [3:0] in_5,
  input  [3:0] Codop,
  output [3:0] Flags,
  output [31:0] S
);

  wire adder_2_cout, and_3_out, and_4_out, and_5_out, and_6_out, CarryOutADC, CarryOutCMN, CarryOutCMP,
       CarryOutRSB, CarryOutSBC, comparator_1_gt, comparator_2_lt, comparator_3_gt, comparator_4_gt,
       comparator_5_eq, not_2_out, or_1_out, or_2_out, subtractor_1_bout, subtractor_2_bout,
       subtractor_3_bout;
  wire [3:0] Codop_t;
  wire [31:0] not_1_out, PARM_ADC, PARM_AND, PARM_ASR, PARM_BIC, PARM_CMN, PARM_CMP, PARM_EOR, PARM_LSL,
       PARM_LSR, PARM_MUL, PARM_MVN, PARM_ORR, PARM_ROR, PARM_RSB, PARM_SBC, PARM_TST;

  assign not_1_out = ~A;  // NOT_Gate not_1, 32 bits wide
  assign PARM_AND = A & B;  // AND_Gate and_1, 32 bits wide
  assign PARM_EOR = A ^ B;  // XOR_Gate xor_1, 32 bits wide
  Shifter #(.width(32)) shifter_1 (.in(B), .\dist (Shift), .out(PARM_LSL));
  Shifter #(.shift("lr"), .width(32)) shifter_2 (.in(B), .\dist (Shift), .out(PARM_LSR));
  Shifter #(.shift("ar"), .width(32)) shifter_3 (.in(B), .\dist (Shift), .out(PARM_ASR));
  assign PARM_BIC = B & not_1_out;  // AND_Gate and_2, 32 bits wide
  Multiplexer #(.select(4), .width(32)) multiplexer_1 (
    .in0(PARM_AND), .in1(PARM_EOR), .in2(PARM_LSL), .in3(PARM_LSR), .in4(PARM_ASR), .in5(PARM_ADC),
    .in6(PARM_SBC), .in7(PARM_ROR), .in8(PARM_TST), .in9(PARM_RSB), .in10(PARM_CMP), .in11(PARM_CMN),
    .in12(PARM_ORR), .in13(PARM_MUL), .in14(PARM_BIC), .in15(PARM_MVN), .out({Flags[3], S[30:0]}), .sel(Codop));
  Comparator #(.width(32)) comparator_1 (.a({32{1'b0}}), .b(B), .gt(comparator_1_gt));  // open: eq, lt
  Comparator #(.width(32)) comparator_2 (.a(A), .b({32{1'b0}}), .lt(comparator_2_lt));  // open: gt, eq
  Comparator #(.width(32)) comparator_3 (.a({32{1'b0}}), .b(B), .gt(comparator_3_gt));  // open: eq, lt
  Comparator #(.width(32)) comparator_4 (.a({32{1'b0}}), .b(A), .gt(comparator_4_gt));  // open: eq, lt
  and and_3 (and_3_out, ~comparator_1_gt, ~comparator_2_lt, Flags[3]);  // AND_Gate
  and and_4 (and_4_out, ~Flags[3], comparator_1_gt, comparator_2_lt);  // AND_Gate
  Comparator #(.width(32)) comparator_5 (.a(A), .b(32'h80000000), .eq(comparator_5_eq));  // open: gt, lt
  and and_5 (and_5_out, ~comparator_3_gt, comparator_4_gt, Flags[3]);  // AND_Gate
  and and_6 (and_6_out, ~Flags[3], comparator_3_gt, ~comparator_4_gt);  // AND_Gate
  Comparator #(.width(32)) comparator_6 (.a({32{1'b0}}), .b({Flags[3], S[30:0]}), .eq(Flags[2]));  // open: gt, lt
  or or_1 (or_1_out, and_3_out, and_4_out);
  or or_2 (or_2_out, and_5_out, and_6_out);
  Multiplexer #(.select(4)) multiplexer_2 (
    .in0(1'b0), .in1(1'b0), .in2(1'b0), .in3(1'b0), .in4(1'b0), .in5(or_1_out), .in6(or_2_out), .in7(1'b0),
    .in8(1'b0), .in9(comparator_5_eq), .in10(or_2_out), .in11(or_1_out), .in12(1'b0), .in13(1'b0),
    .in14(1'b0), .in15(1'b0), .out(Flags[0]), .sel(Codop_t));
  Adder #(.width(32)) adder_1 (.a(A), .b(B), .out(PARM_ADC), .cin(CarryIn), .cout(CarryOutADC));
  not not_2 (not_2_out, CarryIn);
  Subtractor #(.width(32)) subtractor_1 (.a(B), .b(A), .out(PARM_SBC), .bin(not_2_out), .bout(subtractor_1_bout));
  not not_3 (CarryOutSBC, subtractor_1_bout);
  Pull_Resistor pull_resistor_1 (.node(Flags[1]));
  Multiplexer #(.select(4)) multiplexer_3 (
    .in0(CarryOutADC), .in3(CarryOutSBC), .in7(CarryOutRSB), .in11(CarryOutCMP), .out(Flags[1]), .sel(in_5));  // open: in1, in2, in4, in5, in6, in8, in9, in10, in12, in13, in14, in15
  Subtractor #(.width(32)) subtractor_2 (.a({32{1'b0}}), .b(A), .out(PARM_RSB), .bout(subtractor_2_bout));  // open: bin
  assign PARM_MVN = ~A;  // NOT_Gate not_4, 32 bits wide
  Shifter #(.shift("rr"), .width(32)) shifter_4 (.in(B), .\dist (Shift), .out(PARM_ROR));
  assign PARM_TST = A & B;  // AND_Gate and_7, 32 bits wide
  not not_5 (CarryOutRSB, subtractor_2_bout);
  Subtractor #(.width(32)) subtractor_3 (.a(B), .b(A), .out(PARM_CMP), .bout(subtractor_3_bout));  // open: bin
  not not_6 (CarryOutCMP, subtractor_3_bout);
  Adder #(.width(32)) adder_2 (.a(A), .b(B), .out(PARM_CMN), .cout(adder_2_cout));  // open: cin
  not not_7 (CarryOutCMN, adder_2_cout);
  assign PARM_ORR = A | B;  // OR_Gate or_3, 32 bits wide
  Multiplier #(.width(32)) multiplier_1 (.a(A), .b(B), .out(PARM_MUL));  // open: cin, cout

  assign S[31] = Flags[3];
  // also tied to GND on the sheet: Flags[0]

  // Other names for the same wires on the sheet: V = Flags[0]; C = Flags[1]; Z = Flags[2]; N = Flags[3]

  // Notes on the sheet:
  //   Note: for ROR, C = N
  //   Note 2: assume that shift > 0 for LSL and LSR
endmodule
