// Logisim project Ctl_Conditional.circ as structural Verilog: 1 circuit, main circuit Conditional
module Conditional (
  input  Enable,
  input  [15:0] Instruction,
  input  N,
  input  Z,
  input  C,
  input  V,
  output [10:0] Offset,
  output Verified
);

  wire and_1_out, and_3_out, and_4_out, and_5_out, multiplexer_1_out, multiplexer_2_out, not_1_out,
       not_2_out, not_3_out, not_4_out, Uncond, xnor_1_out, xor_1_out;
  wire [10:0] bit_extender_1_out, bit_extender_2_out, multiplexer_3_out;

  not not_1 (not_1_out, Z);
  and and_1 (and_1_out, not_1_out, C);
  // AND_Gate and_2 is placed but not wired
  and and_3 (and_3_out, Z, not_2_out);
  not not_2 (not_2_out, C);
  not not_3 (not_3_out, N);
  xnor xnor_1 (xnor_1_out, N, V);
  and and_4 (and_4_out, not_1_out, xnor_1_out);
  not not_4 (not_4_out, V);
  xor xor_1 (xor_1_out, N, V);
  and and_5 (and_5_out, not_1_out, xor_1_out);
  Comparator #(.width(5)) comparator_1 (.a(5'b11100), .b(Instruction[15:11]), .eq(Uncond));  // open: gt, lt
  Multiplexer #(.select(4)) multiplexer_1 (
    .in0(Z), .in1(not_1_out), .in2(C), .in3(not_2_out), .in4(N), .in5(not_3_out), .in6(V), .in7(not_4_out),
    .in8(and_1_out), .in9(and_3_out), .in10(xnor_1_out), .in11(xor_1_out), .in12(and_4_out),
    .in13(and_5_out), .in14(1'b1), .in15(1'b0), .out(multiplexer_1_out), .sel(Instruction[11:8]));
  assign bit_extender_1_out = {{3{Instruction[7]}}, Instruction[7:0]};  // Bit_Extender bit_extender_1
  Multiplexer multiplexer_2 (.in0(multiplexer_1_out), .in1(1'b1), .out(multiplexer_2_out), .sel(Uncond));
  Multiplexer #(.width(11)) multiplexer_3 (
    .in0(Instruction[10:0]), .in1(bit_extender_1_out), .out(multiplexer_3_out), .sel(Uncond));
  and and_6 (Verified, multiplexer_2_out, Enable);
  assign bit_extender_2_out = {{10{Enable}}, Enable};  // Bit_Extender bit_extender_2
  assign Offset = bit_extender_2_out & multiplexer_3_out;  // AND_Gate and_7, 11 bits wide

  // Other names for the same wires on the sheet: Cond[3:0] = Instruction[11:8]
endmodule
