// Logisim project Ctl_Data_Processing.circ as structural Verilog: 1 circuit, main circuit Data_Processing
module Data_Processing (
  input  [15:0] Instruction,
  input  Enable,
  output [2:0] Rm,
  output [2:0] Rd,
  output [2:0] Rn,
  output [3:0] ALU_Opcode,
  output [3:0] Flags_Update_Mask
);

  wire [2:0] multiplexer_1_out, multiplexer_2_out;
  wire [3:0] multiplexer_5_out;

  Multiplexer #(.select(4), .width(3)) multiplexer_1 (
    .in0(Instruction[2:0]), .in1(Instruction[2:0]), .in2(Instruction[2:0]), .in3(Instruction[2:0]),
    .in4(Instruction[2:0]), .in5(Instruction[2:0]), .in6(Instruction[2:0]), .in7(Instruction[2:0]),
    .in8(Instruction[2:0]), .in9(Instruction[5:3]), .in10(Instruction[2:0]), .in11(Instruction[2:0]),
    .in12(Instruction[2:0]), .in13(Instruction[5:3]), .in14(Instruction[2:0]), .in15(Instruction[2:0]),
    .out(multiplexer_1_out), .sel(Instruction[9:6]));
  Multiplexer #(.select(4), .width(3)) multiplexer_2 (
    .in0(Instruction[5:3]), .in1(Instruction[5:3]), .in2(Instruction[5:3]), .in3(Instruction[5:3]),
    .in4(Instruction[5:3]), .in5(Instruction[5:3]), .in6(Instruction[5:3]), .in7(Instruction[5:3]),
    .in8(Instruction[5:3]), .in10(Instruction[5:3]), .in11(Instruction[5:3]), .in12(Instruction[5:3]),
    .in13(Instruction[2:0]), .in14(Instruction[5:3]), .in15(Instruction[5:3]), .out(multiplexer_2_out),
    .sel(Instruction[9:6]));  // open: in9
  Multiplexer #(.width(3)) multiplexer_3 (.in0(3'b000), .in1(multiplexer_2_out), .out(Rm), .sel(Enable));
  Multiplexer #(.width(3)) multiplexer_4 (.in0(3'b000), .in1(multiplexer_1_out), .out(Rn), .sel(Enable));
  Multiplexer #(.select(4), .width(4)) multiplexer_5 (
    .in0(4'b1110), .in1(4'b1110), .in2(4'b1110), .in3(4'b1110), .in4(4'b1110), .in5(4'b1111), .in6(4'b1111),
    .in7(4'b1110), .in8(4'b1110), .in9(4'b1111), .in10(4'b1111), .in11(4'b1111), .in12(4'b1110),
    .in13(4'b1100), .in14(4'b1110), .in15(4'b1110), .out(multiplexer_5_out), .sel(Instruction[9:6]));
  Multiplexer #(.width(4)) multiplexer_6 (.in0(4'b0000), .in1(Instruction[9:6]), .out(ALU_Opcode), .sel(Enable));
  Multiplexer #(.width(3)) multiplexer_7 (.in0(3'b000), .in1(Instruction[2:0]), .out(Rd), .sel(Enable));
  Multiplexer #(.width(4)) multiplexer_8 (
    .in0(4'b0000), .in1(multiplexer_5_out), .out(Flags_Update_Mask), .sel(Enable));

  // Other names for the same wires on the sheet: Flags[3:0] = Flags_Update_Mask;
  //   Instruction_Rd[2:0] = Instruction[2:0]; Instruction_Rn[2:0] = Instruction[2:0];
  //   Instruction_Rm[2:0] = Instruction[5:3]; ALU[3:0] = Instruction[9:6]

  // Notes on the sheet:
  //   Pull output low on Enable = 0
endmodule
