// Logisim project Ctl_Flags_APSR.circ as structural Verilog: 1 circuit, main circuit Flags_APSR
module Flags_APSR (
  input  [3:0] Update_Mask,
  input  [3:0] Flags_In,
  input  Clk,
  input  Rst,
  output [3:0] Flags_Out
);

  wire MUX_C, MUX_N, MUX_V, MUX_Z;

  Multiplexer multiplexer_1 (.in0(Flags_Out[0]), .in1(Flags_In[0]), .out(MUX_N), .sel(Update_Mask[0]));
  Multiplexer multiplexer_2 (.in0(Flags_Out[1]), .in1(Flags_In[1]), .out(MUX_Z), .sel(Update_Mask[1]));
  Multiplexer multiplexer_3 (.in0(Flags_Out[2]), .in1(Flags_In[2]), .out(MUX_C), .sel(Update_Mask[2]));
  Multiplexer multiplexer_4 (.in0(Flags_Out[3]), .in1(Flags_In[3]), .out(MUX_V), .sel(Update_Mask[3]));
  Register #(.width(1)) register_1 (.D(MUX_Z), .en(Update_Mask[1]), .clk(Clk), .Q(Flags_Out[1]), .clr(Rst));
  Register #(.width(1)) register_2 (.D(MUX_C), .en(Update_Mask[2]), .clk(Clk), .Q(Flags_Out[2]), .clr(Rst));
  Register #(.width(1)) register_3 (.D(MUX_C), .en(Update_Mask[2]), .clk(Clk), .Q(Flags_Out[3]), .clr(Rst));
  Register #(.width(1)) register_4 (.D(MUX_N), .en(Update_Mask[0]), .clk(Clk), .Q(Flags_Out[0]), .clr(Rst));

  // Other names for the same wires on the sheet: IN_N = Flags_In[0]; IN_Z = Flags_In[1]; IN_C = Flags_In[2];
  //   IN_V = Flags_In[3]; OUT_N = Flags_Out[0]; OUT_Z = Flags_Out[1]; OUT_C = Flags_Out[2]; OUT_V = Flags_Out[3];
  //   MASK_N = Update_Mask[0]; MASK_OUT = Update_Mask[0]; SORTIES_MUX = MUX_N; MASK_Z = Update_Mask[1];
  //   MASK_C = Update_Mask[2]; MASK_V = Update_Mask[3]
endmodule
