// Logisim project Ctl_Load_Store.circ as structural Verilog: 1 circuit, main circuit Load_Store
module Load_Store (
  input  Enable,
  input  [15:0] Instruction,
  input  [31:0] Stack_Pointer,
  input  Clk,
  input  Reset,
  output [31:0] RAM_Addr,
  output Load,
  output Store,
  output PC_Hold,
  output [2:0] Rmd
);

  wire and_1_out, bitselector_1_out, comparator_1_gt;
  wire [7:0] bitselector_2_out, bitselector_3_out;
  wire [31:0] adder_1_out, bit_extender_1_out;

  BitSelector #(.width(16)) bitselector_1 (.in(Instruction), .out(bitselector_1_out));  // open: sel
  BitSelector #(.group(8), .width(16)) bitselector_2 (.in(Instruction), .out(bitselector_2_out));  // open: sel
  BitSelector #(.group(8), .width(16)) bitselector_3 (.in(Instruction), .out(bitselector_3_out));  // open: sel
  BitSelector #(.group(3)) bitselector_4 (.in(bitselector_2_out));  // open: out, sel
  assign bit_extender_1_out = {{24{1'b0}}, bitselector_3_out};  // Bit_Extender bit_extender_1
  Comparator #(.width(1)) comparator_1 (.a(bitselector_1_out), .b(1'b0), .gt(comparator_1_gt));  // open: eq, lt
  Adder #(.width(32)) adder_1 (.a(bit_extender_1_out), .b(Stack_Pointer), .out(adder_1_out));  // open: cin, cout
  and and_1 (and_1_out, Enable, Enable);
  Multiplexer multiplexer_1 ();  // open: in0, in1, out, sel
  Multiplexer multiplexer_2 (.in1(comparator_1_gt));  // open: in0, out, sel
  Multiplexer multiplexer_3 ();  // open: in0, in1, out, sel
  Multiplexer #(.width(32)) multiplexer_4 (.in1(adder_1_out), .out(RAM_Addr));  // open: in0, sel
  D_Flip_Flop d_ff_1 (.D(and_1_out), .clk(Clk), .Q(PC_Hold), .reset(Reset));  // open: Qn, preset

  assign Store = Enable;

  // Notes on the sheet:
  //   Instruction: pull=down
endmodule
