// Logisim project Ctl_Shift_Add_Sub_Mov.circ as structural Verilog: 1 circuit, main circuit Shift_Add_Sub_Mov
module Shift_Add_Sub_Mov (
  input  Enable,
  input  [15:0] Instruction,
  output [3:0] Flags_Update_Mask,
  output Carry,
  output Imm32_Enable,
  output [31:0] Imm32,
  output [4:0] Imm5,
  output [2:0] Rm,
  output [2:0] Rn,
  output [2:0] Rd,
  output [3:0] ALU_Opcode
);

  wire and_1_out, comparator_1_eq, comparator_2_eq, multiplexer_5_out, or_1_out;
  wire [2:0] multiplexer_2_out, multiplexer_8_out, multiplexer_9_out, multiplexer_10_out;
  wire [3:0] multiplexer_3_out, multiplexer_4_out, multiplexer_11_out;
  wire [4:0] multiplexer_7_out;
  wire [31:0] bit_extender_1_out, bit_extender_2_out, multiplexer_1_out, multiplexer_6_out, negator_1_out;

  assign bit_extender_1_out = {{29{1'b0}}, Instruction[8:6]};  // Bit_Extender bit_extender_1
  Multiplexer #(.width(32)) multiplexer_1 (
    .in0({32{1'b0}}), .in1(bit_extender_1_out), .out(multiplexer_1_out), .sel(Instruction[10]));
  assign bit_extender_2_out = {{24{1'b0}}, Instruction[7:0]};  // Bit_Extender bit_extender_2
  Multiplexer #(.width(3)) multiplexer_2 (
    .in0(Instruction[8:6]), .in1(3'b000), .out(multiplexer_2_out), .sel(Instruction[10]));
  Comparator #(.width(3)) comparator_1 (.a(Instruction[13:11]), .b(3'b011), .eq(comparator_1_eq));  // open: gt, lt
  Comparator #(.width(3)) comparator_2 (.a(Instruction[13:11]), .b(3'b111), .eq(comparator_2_eq));  // open: gt, lt
  Negator #(.width(32)) negator_1 (.in(bit_extender_2_out), .out(negator_1_out));
  Multiplexer #(.width(4)) multiplexer_3 (.in0(4'b0101), .in1(4'b0110), .out(multiplexer_3_out), .sel(Instruction[9]));
  Multiplexer #(.select(3), .width(4)) multiplexer_4 (
    .in0(4'b1110), .in1(4'b1110), .in2(4'b1110), .in3(4'b1111), .in4(4'b1100), .in5(4'b1111), .in6(4'b1111),
    .in7(4'b1111), .out(multiplexer_4_out), .sel(Instruction[13:11]));
  and and_1 (and_1_out, comparator_1_eq, Instruction[9]);
  or or_1 (or_1_out, and_1_out, comparator_2_eq);
  Multiplexer #(.select(3)) multiplexer_5 (
    .in0(1'b0), .in1(1'b0), .in2(1'b0), .in3(Instruction[10]), .in4(1'b1), .in5(1'b1), .in6(1'b1),
    .in7(1'b1), .out(multiplexer_5_out), .sel(Instruction[13:11]));
  Multiplexer #(.select(3), .width(32)) multiplexer_6 (
    .in0({32{1'b0}}), .in1({32{1'b0}}), .in2({32{1'b0}}), .in3(multiplexer_1_out), .in4(negator_1_out),
    .in5(bit_extender_2_out), .in6(bit_extender_2_out), .in7(bit_extender_2_out), .out(multiplexer_6_out),
    .sel(Instruction[13:11]));
  Multiplexer #(.select(3), .width(5)) multiplexer_7 (
    .in0(Instruction[10:6]), .in1(Instruction[10:6]), .in2(Instruction[10:6]), .in3({5{1'b0}}),
    .in4({5{1'b0}}), .in5({5{1'b0}}), .in6({5{1'b0}}), .in7({5{1'b0}}), .out(multiplexer_7_out),
    .sel(Instruction[13:11]));
  Multiplexer #(.select(3), .width(3)) multiplexer_8 (
    .in0(Instruction[5:3]), .in1(Instruction[5:3]), .in2(Instruction[5:3]), .in3(multiplexer_2_out),
    .in4(3'b000), .in5(3'b000), .in6(3'b000), .in7(3'b000), .out(multiplexer_8_out), .sel(Instruction[13:11]));
  Multiplexer #(.select(3), .width(3)) multiplexer_9 (
    .in0(Instruction[5:3]), .in1(Instruction[5:3]), .in2(Instruction[5:3]), .in3(Instruction[5:3]),
    .in4(3'b000), .in5(3'b000), .in6(Instruction[10:8]), .in7(Instruction[10:8]), .out(multiplexer_9_out),
    .sel(Instruction[13:11]));
  Multiplexer #(.select(3), .width(3)) multiplexer_10 (
    .in0(Instruction[2:0]), .in1(Instruction[2:0]), .in2(Instruction[2:0]), .in3(Instruction[2:0]),
    .in4(Instruction[10:8]), .in5(Instruction[10:8]), .in6(Instruction[10:8]), .in7(Instruction[10:8]),
    .out(multiplexer_10_out), .sel(Instruction[13:11]));
  Multiplexer #(.select(3), .width(4)) multiplexer_11 (
    .in0(4'b0010), .in1(4'b0011), .in2(4'b0100), .in3(multiplexer_3_out), .in4(4'b1001), .in5(4'b1010),
    .in6(4'b0101), .in7(4'b0110), .out(multiplexer_11_out), .sel(Instruction[13:11]));
  Multiplexer #(.width(4)) multiplexer_12 (
    .in0(4'b0000), .in1(multiplexer_4_out), .out(Flags_Update_Mask), .sel(Enable));
  Multiplexer multiplexer_13 (.in0(1'b0), .in1(or_1_out), .out(Carry), .sel(Enable));
  Multiplexer multiplexer_14 (.in0(1'b0), .in1(multiplexer_5_out), .out(Imm32_Enable), .sel(Enable));
  Multiplexer #(.width(32)) multiplexer_15 (.in0({32{1'b0}}), .in1(multiplexer_6_out), .out(Imm32), .sel(Enable));
  Multiplexer #(.width(5)) multiplexer_16 (.in0({5{1'b0}}), .in1(multiplexer_7_out), .out(Imm5), .sel(Enable));
  Multiplexer #(.width(3)) multiplexer_17 (.in0(3'b000), .in1(multiplexer_8_out), .out(Rm), .sel(Enable));
  Multiplexer #(.width(3)) multiplexer_18 (.in0(3'b000), .in1(multiplexer_9_out), .out(Rn), .sel(Enable));
  Multiplexer #(.width(3)) multiplexer_19 (.in0(3'b000), .in1(multiplexer_10_out), .out(Rd), .sel(Enable));
  Multiplexer #(.width(4)) multiplexer_20 (.in0(4'b0000), .in1(multiplexer_11_out), .out(ALU_Opcode), .sel(Enable));

  // Other names for the same wires on the sheet: b6 = Instruction[6]; b7 = Instruction[7]; b3 = Instruction[3];
  //   b4 = Instruction[4]; b5 = Instruction[5]; b0 = Instruction[0]; b1 = Instruction[1]; b2 = Instruction[2];
  //   b8 = Instruction[8]; b9 = Instruction[9]; b10 = Instruction[10]; opcode[2:0] = Instruction[13:11]

  // Notes on the sheet:
  //   Pull output low on Enable = 0
  //   Note: ALU uses Rn register for shifts. Use Rn instead of Rm for shifts (immediate) here too
  //   Note 2: MOV uses RSB ALU opcode with Imm8 reversed so that it is copied to output register
  //   Note 3: Imm32_Enable forces the use of the immediate for Rm register
  //   only ADD and SUB use Rm
  //   Enable carry for SUB since it is reversed in ALU
  //   ALU will use Imm32 instead of Rm
endmodule
